# Fritzing sketch pcb final product (saved by Fritzing 0.9.9b)
circuit board: 6.4cm x 5.6cm
breadboards: 1

parts:
  R2_1kΩ = Resistor [tolerance=±5% resistance=1k package="0805 [SMD]"]
  led = male pin header, 2 pins [form="♂ (male)"]
  SR04_(vcc_trig_echo_gnd) = male pin header, 4 pins [form="♂ (male)"]
  R3_2_2kΩ = Resistor [tolerance=±5% power=0.25 resistance=2.2k package=THT]
  R4_220Ω = Resistor [tolerance=±5% power=0.25 resistance=220 package=THT]
  Raspberry_Pi_1 = Raspberry Pi 3 [part_number=RPI-3-V1.2]

nets:
  N1: R2_1kΩ.Pin_0, R2_1kΩ.Pin_1, SR04_(vcc_trig_echo_gnd).pin3, R3_2_2kΩ.Pin_0, Raspberry_Pi_1.GIPO17
  N2: led.pin1, Raspberry_Pi_1.GIPO18
  N3: led.pin2, R4_220Ω.Pin_0
  N4: SR04_(vcc_trig_echo_gnd).pin1, Raspberry_Pi_1.5V
  N5: SR04_(vcc_trig_echo_gnd).pin2, Raspberry_Pi_1.GIPO4
  N6: SR04_(vcc_trig_echo_gnd).pin4, R3_2_2kΩ.Pin_1, R4_220Ω.Pin_1, Raspberry_Pi_1.GND
